# Fritzing sketch photogrammetry-turntable (saved by Fritzing 0.9.6b)
circuit board: 6.71313cm x 3.51379cm
breadboards: 1

parts:
  DRV_1 = DRV 8825 Stepper Motor Carrier, High Current [part_number="DRV 8825"]
  C1 = Electrolytic Capacitor [capacitance=100µF voltage=35V package="200 mil [THT, electrolytic]"]  # not connected
  M1 = Stepper Motor - Bipolar  # not connected
  Part1 = Arduino Uno (Rev3) - ICSP
  Q1 = TRANSISTOR_NPN [package=to-92-ammo]
  LED1 = LEDs [package=led10mm]
  R1 = Resistor [tolerance=±5% resistance=470 package="2010 [SMD]"]

nets:
  N1: DRV_1.RESET, Part1.5V, Q1.C
  N2: Part1.D6_PWM, R1.Pin_0
  N3: Part1.GND, LED1.A
  N4: Q1.E, LED1.C
  N5: Q1.B, R1.Pin_1

notes:
  LED1 = IR TX LED
  R1 = 470 ohm resister
  T1 = 2N2222
  C1 = 100 µF
  Motor = NEMA17
